# Fritzing sketch Circuit Diagram (saved by Fritzing 0.9.3b)
breadboards: 1

parts:
  Part1 = Arduino Mega 2560 (Rev3)
  Gizwits_WiFi_Witty_ESP-12F1 = Gizwits WiFi Witty ESP-12F
  Part2 = Logic Level Converter
  WeMos_D1_Mini_OLED_Shield1 = WeMos D1 Mini OLED Shield
  Part3 = Real Time Clock Module - DS1307 RTC Breakout Board
  Part4 = Ludus ProtoShield
  R1 = Trimmer Potentiometer [maximum_resistance=10kΩ package=THT]
  R2 = Trimmer Potentiometer [maximum_resistance=10kΩ package=THT]
  S1 = Momentary Switch [package=ksa_sealed_tac_switch]
  S2 = Momentary Switch [package=ksa_sealed_tac_switch]
  S3 = Momentary Switch [package=ksa_sealed_tac_switch]
  S4 = Momentary Switch [package=ksa_sealed_tac_switch]
  R3 = Resistor [tolerance=±5% resistance=220 package="1206 [SMD]"]
  R4 = Resistor [tolerance=±5% resistance=220 package="1206 [SMD]"]
  R5 = Resistor [tolerance=±5% resistance=220 package="1206 [SMD]"]
  R6 = Resistor [tolerance=±5% resistance=220 package="1206 [SMD]"]

nets:
  N1: Part1.A6, R1.wiper
  N2: Part1.A7, R2.wiper
  N3: Part1.D21/SCL, WeMos_D1_Mini_OLED_Shield1.D0, Part3.SCL, Part4.SCL
  N4: Part1.D20/SDA, WeMos_D1_Mini_OLED_Shield1.A0, Part3.SDA, Part4.SDA
  N5: Part1.D19/RX1, Part2.TX_HV
  N6: Part1.D18/TX1, Part2.RX_HV
  GND: Part1.GND, Gizwits_WiFi_Witty_ESP-12F1.GND, Part2.GND, WeMos_D1_Mini_OLED_Shield1.G, Part3.GND, Part4.GND, R3.Pin_1, R4.Pin_1, R5.Pin_1, R6.Pin_1
  N7: Part1.3V3, Part2.LV
  5V: Part1.5V, Part3.5V
  VCC: Part1.VIN, Gizwits_WiFi_Witty_ESP-12F1.VCC, Part2.HV, WeMos_D1_Mini_OLED_Shield1.5V, Part4.VCC
  N8: Part1.D22, S3.3, R3.Pin_0
  N9: Part1.D24, S4.3, R4.Pin_0
  N10: Part1.D26, S2.3, R6.Pin_0
  N11: Part1.D28, S1.3, R5.Pin_0
  N12: Gizwits_WiFi_Witty_ESP-12F1.RXD, Part2.RX_LV
  N13: Gizwits_WiFi_Witty_ESP-12F1.TXD, Part2.TX_LV
  N14: R1.leg1, R2.leg1
  N15: R1.leg2, R2.leg2, S1.2, S2.2, S3.2, S4.2
